# Fritzing sketch 2D plotter (saved by Fritzing 1.0.4)
breadboards: 1

parts:
  DRV_1 = DRV 8825 Stepper Motor Carrier, High Current [part_number="DRV 8825"]
  DRV_2 = DRV 8825 Stepper Motor Carrier, High Current [part_number="DRV 8825"]
  J1-12V = Power Jack [package=power_jack_slot]
  F1 = FUSE [package=fuse_5mm]
  C2 = Electrolytic Capacitor [capacitance=100µF voltage=35V package="200 mil [THT, electrolytic]"]
  C3 = Electrolytic Capacitor [capacitance=100µF voltage=35V package="200 mil [THT, electrolytic]"]
  LED1_power = LED - 3mm [color="Red (633nm)" current=0.030A package="3 mm [THT]"]
  R1 = Resistor [tolerance=±5% resistance=220 package="2010 [SMD]"]
  C4 = Electrolytic Capacitor [capacitance=1000μF voltage=35V package="1010 [SMD, electrolytic]"]
  C5 = Electrolytic Capacitor [capacitance=1000μF voltage=35V package="1010 [SMD, electrolytic]"]
  C6_104 = Capacitor [package=cap-pth-small2]
  C6_105 = Capacitor [package=cap-pth-small2]
  DC1 = Hirose DF13 Series Header [part_number=DF13#-4P-1.25V package=DF13C-4P-1.25V]
  DC2 = Hirose DF13 Series Header [part_number=DF13#-4P-1.25V package=DF13C-4P-1.25V]
  R2ctht_10k = Resistor [tolerance=±5% resistance=220 package="2512 [SMD]"]
  R2ctht_10k1 = Resistor [tolerance=±5% resistance=220 package="2512 [SMD]"]
  SW1 = DIP Switch 8 Position [package=dipswitch-08]
  servo = Hirose DF13 Series Header [part_number=DF13A-3P-1.25H package=DF13A-3P-1.25H]
  M1 = RioRand LM2596
  Linh_kiện1 = Adafruit DS1307 RTC Breakout [part_number="Adafruit #264"]
  R2ctht_10k2 = Resistor [tolerance=±5% resistance=220 package="2512 [SMD]"]
  R2ctht_10k3 = Resistor [tolerance=±5% resistance=220 package="2512 [SMD]"]
  R2ctht_10k4 = Resistor [tolerance=±5% resistance=220 package="2512 [SMD]"]
  R2ctht_10k5 = Resistor [tolerance=±5% resistance=220 package="2512 [SMD]"]
  R2ctht_10k6 = Resistor [tolerance=±5% resistance=220 package="2512 [SMD]"]
  R2ctht_10k7 = Resistor [tolerance=±5% resistance=220 package="2512 [SMD]"]
  U1 = LuaNode32 / ESP32
  U4 = Hirose DF13 Series Header [part_number=DF13#-6P-1.25V package=DF13C-6P-1.25V]
  M2 = pcf8574 io expansion board [package=THT]
  EXP1 = Header 5x2 [package=2x5-shrouded_smd]
  U5 = Hirose DF13 Series Header [part_number=DF13#-2P-1.25V package=DF13C-2P-1.25V]
  U6 = Hirose DF13 Series Header [part_number=DF13#-2P-1.25V package=DF13C-2P-1.25V]
  EXP2 = Header 5x2 [package=2x5-shrouded_smd]

nets:
  GND: DRV_1.ENABLE, DRV_1.GROUND_ST/_MT, DRV_1.GROUND_LOG, DRV_2.ENABLE, J1-12V.GNDBREAK, J1-12V.GND, C2.-, LED1_power.cathode, C4.-, C5.-, C6_104.2, C6_105.2, servo.1, M1.Pin_2, M1.Pin_4, Linh_kiện1.GND, R2ctht_10k2.Pin_1, R2ctht_10k3.Pin_1, R2ctht_10k4.Pin_1, R2ctht_10k5.Pin_1, R2ctht_10k6.Pin_1, R2ctht_10k7.Pin_1, U1.GND, U4.1, M2.GND, EXP1.9, U5.2, U6.2, EXP2.8
  N1: DRV_1.MS1, SW1.3, R2ctht_10k7.Pin_0
  N2: DRV_1.MS2, SW1.2, R2ctht_10k3.Pin_0
  N3: DRV_1.MS3, SW1.1, R2ctht_10k2.Pin_0
  VCC: DRV_1.RESET, DRV_1.SLEEP, DRV_1.VOLTAGE_DD, DRV_2.RESET, DRV_2.SLEEP, DRV_2.VOLTAGE_DD, R1.Pin_0, C6_105.1, R2ctht_10k.Pin_0, R2ctht_10k1.Pin_1, SW1.11, SW1.12, SW1.13, SW1.14, SW1.15, SW1.16, servo.3, Linh_kiện1.VCC, U1.Vin, U4.3, M2.VCC, EXP1.10
  N4: DRV_1.STEP, U1.D35
  N5: DRV_1.DIRECTION, U1.D34
  N6: DRV_1.VOLTAGE_ST/_MT, F1.2, C2.+, C4.+, C6_104.1, M1.Pin_1
  N7: DRV_1.OUT_2B, DC1.1
  N8: DRV_1.OUT_2A, DC1.2
  N9: DRV_1.OUT_1A, DC1.3
  N10: DRV_1.OUT_1B, DC1.4
  N11: DRV_2.MS1, SW1.6, R2ctht_10k4.Pin_0
  N12: DRV_2.MS2, SW1.5, R2ctht_10k5.Pin_0
  N13: DRV_2.MS3, SW1.4, R2ctht_10k6.Pin_0
  N14: DRV_2.STEP, U1.D4
  N15: DRV_2.DIRECTION, U1.D2
  N16: DRV_2.VOLTAGE_ST/_MT, C3.+
  N17: DRV_2.GROUND_ST/_MT, DRV_2.GROUND_LOG, C3.-
  N18: DRV_2.OUT_2B, DC2.1
  N19: DRV_2.OUT_2A, DC2.2
  N20: DRV_2.OUT_1A, DC2.3
  N21: DRV_2.OUT_1B, DC2.4
  N22: J1-12V.PWR, F1.1
  N23: LED1_power.anode, R1.Pin_1
  N24: C5.+, M1.Pin_3
  N25: R2ctht_10k.Pin_1, U1.D26, U5.1
  N26: R2ctht_10k1.Pin_0, U1.D27, U6.1
  N27: Linh_kiện1.SCL, U1.D22, M2.SCL
  N28: Linh_kiện1.SDA, U1.D21, M2.SDA
  N29: U1.EN, U4.6
  N30: U1.D32, EXP2.3
  N31: U1.D33, EXP2.5
  N32: U1.D25, EXP2.4
  N33: U1.RX2, U4.4
  N34: U1.TX2, U4.5
  N35: U1.D18, EXP2.2
  N36: U1.D19, EXP2.1
  N37: U1.D23, EXP2.6
  N38: M2.O0, EXP1.1
  N39: M2.O1, EXP1.2
  N40: M2.O2, EXP1.4
  N41: M2.O3, EXP1.5
  N42: M2.O4, EXP1.6
  N43: M2.O5, EXP1.7
  N44: M2.O6, EXP1.8
  N45: M2.O7, EXP1.3

notes:
  P0Beeper P1 Encoder click
  P2 RS P3 DB4
  P4 DB5 P5 DB6
  P6 DB7 P7 EN
  I2c: SCL GPIO22,SDA21
  SPI:
  -miso: gpio19
  -mosi :gpio 23
  -CLK: gpio 18
  -GND
  -CTS
  -VCC (FT232)
  -TX
  -RX
  -DTR
  EXP1
  1)beep 2)Encoder click
  3)EN 4)RS 5)DB4 6)DB5
  7)DB6 8)DB7 9) GND 10) VCC
  EXP2
  1)DOUT(miso) 2)CLK
  3)EN2 4)CS 5)EN1 6)DIN(mosi)
  7)CMD 8)RST 9) NC 10)NC

custom parts:
  Adafruit DS1307 RTC Breakout: This is a great battery-backed real time clock (RTC) that allows your microcontroller project to keep track of time even if it is reprogrammed, or if the power is lost. Perfect for datalogging, clock-building, time stamping, timers and alarms, etc. The DS1307 is the most popular RTC - but it requires 5V power to work (although we've used it with 5V power and 3.3V logic successfully) PCB &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
  LuaNode32 / ESP32: ESP32 based LuaNode32
  pcf8574 io expansion board: pcf8574 io expansion board.
