# Fritzing sketch 2D plotter (saved by Fritzing 1.0.4)
breadboards: 1

parts:
  DRV_1 = DRV 8825 Stepper Motor Carrier, High Current [part_number="DRV 8825"]
  DRV_2 = DRV 8825 Stepper Motor Carrier, High Current [part_number="DRV 8825"]
  J1-12V = Power Jack [package=power_jack_slot]
  F1 = FUSE [package=fuse_5mm]
  C2 = Electrolytic Capacitor [capacitance=100µF voltage=35V package="200 mil [THT, electrolytic]"]
  C3 = Electrolytic Capacitor [capacitance=100µF voltage=35V package="200 mil [THT, electrolytic]"]
  LED1_power = LED - 3mm [color="Red (633nm)" current=0.030A package="3 mm [THT]"]
  R1 = Resistor [tolerance=±5% resistance=220 package="2010 [SMD]"]
  C4 = Electrolytic Capacitor [capacitance=1000μF voltage=35V package="1010 [SMD, electrolytic]"]
  C5 = Electrolytic Capacitor [capacitance=1000μF voltage=35V package="1010 [SMD, electrolytic]"]
  C6_104 = Capacitor [package=cap-pth-small2]
  C6_105 = Capacitor [package=cap-pth-small2]
  DC1 = Hirose DF13 Series Header [part_number=DF13#-4P-1.25V package=DF13C-4P-1.25V]
  DC2 = Hirose DF13 Series Header [part_number=DF13#-4P-1.25V package=DF13C-4P-1.25V]
  R2ctht_10k = Resistor [tolerance=±5% resistance=220 package="2512 [SMD]"]
  J3 = Camdenboss CTB0158-2 [part_number=CTB0158-2 package=THT]
  R2ctht_10k1 = Resistor [tolerance=±5% resistance=220 package="2512 [SMD]"]
  J4 = Camdenboss CTB0158-2 [part_number=CTB0158-2 package=THT]
  SW1 = DIP Switch 8 Position [package=dipswitch-08]
  servo = Hirose DF13 Series Header [part_number=DF13A-3P-1.25H package=DF13A-3P-1.25H]
  U1 = ESP32-38PinWide [part_number=ESP32-38PinWide]
  Mod1 = KY-023 Dual Axis Joystick Module [package="Breakout board"]
  SG1 = Buzzer 12mm [package=buzzer-ccv-kit]
  Q2 = TRANSISTOR_NPN [package=to-92]
  tro1k = Resistor [tolerance=±5% resistance=220 package="2512 [SMD]"]
  RE1 = KY-040 Rotary encoder [package=THT]
  LCD2004-i2C = Hirose DF13 Series Header [part_number=DF13#-4P-1.25V package=DF13C-4P-1.25V]
  sdCard1 = my_sdCard
  M1 = RioRand LM2596
  Linh_kiện1 = Adafruit DS1307 RTC Breakout [part_number="Adafruit #264"]

nets:
  N1: DRV_1.MS1, SW1.3
  N2: DRV_1.MS2, SW1.2
  N3: DRV_1.MS3, SW1.1
  N4: DRV_1.RESET, DRV_1.SLEEP
  N5: DRV_1.STEP, U1.GPIO4
  N6: DRV_1.DIRECTION, U1.GPIO0
  N7: DRV_1.VOLTAGE_ST/_MT, F1.2, C2.+, C4.+, C6_104.1, M1.Pin_1
  N8: DRV_1.GROUND_ST/_MT, DRV_1.GROUND_LOG, J1-12V.GNDBREAK, J1-12V.GND, C2.-, LED1_power.cathode, C4.-, C5.-, C6_104.2, C6_105.2, servo.1, M1.Pin_2, M1.Pin_4
  N9: DRV_1.OUT_2B, DC1.1
  N10: DRV_1.OUT_2A, DC1.2
  N11: DRV_1.OUT_1A, DC1.3
  N12: DRV_1.OUT_1B, DC1.4
  VCC: DRV_1.VOLTAGE_DD, DRV_2.VOLTAGE_DD, R1.Pin_0, C6_105.1, R2ctht_10k.Pin_0, R2ctht_10k1.Pin_1, servo.3, U1.VIN, Mod1.+5V, RE1.Vcc, Linh_kiện1.VCC
  N13: DRV_2.MS1, SW1.6
  N14: DRV_2.MS2, SW1.5
  N15: DRV_2.MS3, SW1.4
  N16: DRV_2.RESET, DRV_2.SLEEP
  N17: DRV_2.STEP, U1.GPIO7
  N18: DRV_2.DIRECTION, U1.GPIO6
  N19: DRV_2.VOLTAGE_ST/_MT, C3.+
  N20: DRV_2.GROUND_ST/_MT, DRV_2.GROUND_LOG, C3.-
  N21: DRV_2.OUT_2B, DC2.1
  N22: DRV_2.OUT_2A, DC2.2
  N23: DRV_2.OUT_1A, DC2.3
  N24: DRV_2.OUT_1B, DC2.4
  N25: J1-12V.PWR, F1.1
  N26: LED1_power.anode, R1.Pin_1, SW1.11, SW1.12, SW1.13, SW1.14, SW1.15, SW1.16
  N27: C5.+, M1.Pin_3
  N28: R2ctht_10k.Pin_1, J3.pin1, U1.GPIO17
  N29: J3.pin2, J4.pin2, Q2.E, LCD2004-i2C.2
  N30: R2ctht_10k1.Pin_0, J4.pin1, U1.GPIO16
  N31: servo.2, U1.GPIO8
  N32: U1.3.3, sdCard1.VCC
  N33: U1.GPIO36, RE1.SW
  N34: U1.GPIO39, RE1.DT
  N35: U1.GPIO34, RE1.CLK
  N36: U1.GPIO35, Mod1.VRx
  N37: U1.GPIO32, Mod1.VRy
  N38: U1.GPIO33, Mod1.SW
  GND: U1.GND, Mod1.GND, RE1.GND, sdCard1.GND, Linh_kiện1.GND
  N39: U1.GPIO5, tro1k.Pin_1
  N40: U1.GPIO18, sdCard1.SCK
  N41: U1.GPIO19, sdCard1.MISO
  N42: U1.GPIO21, LCD2004-i2C.4, Linh_kiện1.SDA
  N43: U1.GPIO22, LCD2004-i2C.3, Linh_kiện1.SCL
  N44: U1.GPIO23, sdCard1.MOSI
  N45: SG1.1, LCD2004-i2C.1
  N46: SG1.2, Q2.C
  N47: Q2.B, tro1k.Pin_0

notes:
  I2c: SCL GPIO22,SDA21
  SPI:
  -miso: gpio19
  -mosi :gpio 23
  -sck: gpio 18

custom parts:
  ESP32-38PinWide: Generic 38-Pin ESP32 with wide format (only access to one side of pins on a breadboard) based on Stephen Lilley's HiLetgo ESP-WROOM-32 ESP32 ESP-32S Development Board.
  KY-023 Dual Axis Joystick Module: KY-023 Dual-Axis Joystick Module.
  KY-040 Rotary encoder: KY-040 Rotary Encoder with switch on breakout borad from AZ Delivery
  my_sdCard: micro sdCard Adapter with 90º pin header. Use a filtering Capacitor between CS and GND if needed. PCB View Pinouts are Reversed for laying parallel on PCB using a 90º pin header.
  Adafruit DS1307 RTC Breakout: This is a great battery-backed real time clock (RTC) that allows your microcontroller project to keep track of time even if it is reprogrammed, or if the power is lost. Perfect for datalogging, clock-building, time stamping, timers and alarms, etc. The DS1307 is the most popular RTC - but it requires 5V power to work (although we've used it with 5V power and 3.3V logic successfully) PCB &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
